// Logisim project 2.circ as structural Verilog: 2 circuits, main circuit main
module main (
);

  wire A_q, A_qn, and_1_out, B_q, C_q, clock_1_out, D_q, D_qn, n7seg_2_1_a, n7seg_2_1_b, n7seg_2_1_c,
       n7seg_2_1_d, n7seg_2_1_e, n7seg_2_1_f, n7seg_2_1_g;

  Clock clock_1 (.out(clock_1_out));
  and and_1 (and_1_out, D_qn, C_q);
  J_K_Flip_Flop A (.J(and_1_out), .clk(clock_1_out), .K(1'b0), .Q(A_q), .Qn(A_qn));  // open: preset, en, reset
  J_K_Flip_Flop B (.J(A_qn), .clk(clock_1_out), .K(C_q), .Q(B_q));  // open: Qn, preset, en, reset
  J_K_Flip_Flop C (.J(1'b1), .clk(clock_1_out), .K(1'b1), .Q(C_q));  // open: Qn, preset, en, reset
  J_K_Flip_Flop D (.J(C_q), .clk(clock_1_out), .K(A_qn), .Q(D_q), .Qn(D_qn));  // open: preset, en, reset
  _7seg_2 u_7seg_2_1 (
    .BIT3(A_q), .BIT2(B_q), .BIT1(C_q), .BIT0(D_q), .A(n7seg_2_1_a), .B(n7seg_2_1_b), .C(n7seg_2_1_c),
    .D(n7seg_2_1_d), .E(n7seg_2_1_e), .F(n7seg_2_1_f), .G(n7seg_2_1_g));
  _7_Segment_Display u_7_segment_display_1 (
    .g(n7seg_2_1_a), .f(n7seg_2_1_b), .a(n7seg_2_1_c), .b(n7seg_2_1_d), .e(n7seg_2_1_g), .d(n7seg_2_1_f),
    .c(n7seg_2_1_e));  // open: dp
endmodule

module _7seg_2 (
  input  BIT3,
  input  BIT2,
  input  BIT1,
  input  BIT0,
  output A,
  output B,
  output C,
  output D,
  output E,
  output F,
  output G
);

  wire and_1_out, not_1_out, not_2_out, not_5_out, not_6_out;

  not not_1 (not_1_out, BIT3);
  or or_1 (A, not_1_out, not_2_out);
  not not_2 (not_2_out, BIT2);
  not not_3 (B, BIT1);
  not not_4 (D, BIT2);
  not not_5 (not_5_out, BIT2);
  and and_1 (and_1_out, not_5_out, not_6_out);
  not not_6 (not_6_out, BIT1);
  not not_7 (G, BIT0);
  or or_2 (E, and_1_out, BIT0);

  assign C = 1'b1;
  assign F = 1'b1;
endmodule
