// Logisim project 3.circ as structural Verilog: 3 circuits, main circuit main
module main (
);

  wire clock_1_out, contador_9_0_1_a, contador_9_0_1_b, contador_9_0_1_c, contador_9_0_1_d, contador_9_0_1_e,
       contador_9_0_1_f, contador_9_0_1_g, contador_9_0_2_a, contador_9_0_2_b, contador_9_0_2_c,
       contador_9_0_2_d, contador_9_0_2_e, contador_9_0_2_f, contador_9_0_2_g, contador_9_0_3_a,
       contador_9_0_3_b, contador_9_0_3_c, contador_9_0_3_d, contador_9_0_3_e, contador_9_0_3_f,
       contador_9_0_3_g, n7seg_1_bit0, n7seg_1_bit1, n7seg_1_bit2, n7seg_1_bit3, n7seg_1_out_2, n7seg_2_bit0,
       n7seg_2_bit1, n7seg_2_bit2, n7seg_2_bit3, n7seg_3_bit0, n7seg_3_bit1, n7seg_3_bit2, n7seg_3_bit3,
       n7seg_3_out_2;

  Clock clock_1 (.out(clock_1_out));
  _7seg u_7seg_1 (
    .out_2(n7seg_1_out_2), .Bit0(n7seg_1_bit0), .BIT1(n7seg_1_bit1), .BIT2(n7seg_1_bit2), .BIT3(n7seg_1_bit3));  // open: in_1
  Contador_9_0 contador_9_0_1 (
    .BIT3(n7seg_1_bit3), .BIT2(n7seg_1_bit2), .BIT1(n7seg_1_bit1), .BIT0(n7seg_1_bit0), .A(contador_9_0_1_a),
    .B(contador_9_0_1_b), .C(contador_9_0_1_c), .D(contador_9_0_1_d), .E(contador_9_0_1_e),
    .F(contador_9_0_1_f), .G(contador_9_0_1_g));
  _7seg u_7seg_2 (
    .out_2(n7seg_1_out_2), .in_1(n7seg_3_out_2), .Bit0(n7seg_2_bit0), .BIT1(n7seg_2_bit1),
    .BIT2(n7seg_2_bit2), .BIT3(n7seg_2_bit3));
  Contador_9_0 contador_9_0_2 (
    .BIT3(n7seg_2_bit3), .BIT2(n7seg_2_bit2), .BIT1(n7seg_2_bit1), .BIT0(n7seg_2_bit0), .A(contador_9_0_2_a),
    .B(contador_9_0_2_b), .C(contador_9_0_2_c), .D(contador_9_0_2_d), .E(contador_9_0_2_e),
    .F(contador_9_0_2_f), .G(contador_9_0_2_g));
  _7seg u_7seg_3 (
    .out_2(n7seg_3_out_2), .in_1(clock_1_out), .Bit0(n7seg_3_bit0), .BIT1(n7seg_3_bit1), .BIT2(n7seg_3_bit2),
    .BIT3(n7seg_3_bit3));
  Contador_9_0 contador_9_0_3 (
    .BIT3(n7seg_3_bit3), .BIT2(n7seg_3_bit2), .BIT1(n7seg_3_bit1), .BIT0(n7seg_3_bit0), .A(contador_9_0_3_a),
    .B(contador_9_0_3_b), .C(contador_9_0_3_c), .D(contador_9_0_3_d), .E(contador_9_0_3_e),
    .F(contador_9_0_3_f), .G(contador_9_0_3_g));
  _7_Segment_Display u_7_segment_display_1 (
    .g(contador_9_0_1_a), .f(contador_9_0_1_b), .a(contador_9_0_1_c), .b(contador_9_0_1_d),
    .e(contador_9_0_1_g), .d(contador_9_0_1_f), .c(contador_9_0_1_e));  // open: dp
  _7_Segment_Display u_7_segment_display_2 (
    .g(contador_9_0_2_a), .f(contador_9_0_2_b), .a(contador_9_0_2_c), .b(contador_9_0_2_d),
    .e(contador_9_0_2_g), .d(contador_9_0_2_f), .c(contador_9_0_2_e));  // open: dp
  _7_Segment_Display u_7_segment_display_3 (
    .g(contador_9_0_3_a), .f(contador_9_0_3_b), .a(contador_9_0_3_c), .b(contador_9_0_3_d),
    .e(contador_9_0_3_g), .d(contador_9_0_3_f), .c(contador_9_0_3_e));  // open: dp
endmodule

module _7seg (
  input  in_1,
  output out_2,
  output Bit0,
  output BIT1,
  output BIT2,
  output BIT3
);

  wire contador_9_0_1_a, contador_9_0_1_b, contador_9_0_1_c, contador_9_0_1_d, contador_9_0_1_e,
       contador_9_0_1_f, contador_9_0_1_g, j_k_ff_1_qn, j_k_ff_2_qn, j_k_ff_3_qn;

  Contador_9_0 contador_9_0_1 (
    .BIT3(BIT3), .BIT2(BIT2), .BIT1(BIT1), .BIT0(Bit0), .A(contador_9_0_1_a), .B(contador_9_0_1_b),
    .C(contador_9_0_1_c), .D(contador_9_0_1_d), .E(contador_9_0_1_e), .F(contador_9_0_1_f),
    .G(contador_9_0_1_g));
  _7_Segment_Display u_7_segment_display_1 (
    .g(contador_9_0_1_a), .f(contador_9_0_1_b), .a(contador_9_0_1_c), .b(contador_9_0_1_d),
    .e(contador_9_0_1_g), .d(contador_9_0_1_f), .c(contador_9_0_1_e));  // open: dp
  and and_1 (out_2, BIT3, BIT1);
  J_K_Flip_Flop j_k_ff_1 (
    .J(1'b1), .clk(in_1), .K(1'b1), .Q(Bit0), .Qn(j_k_ff_1_qn), .reset(out_2));  // open: preset, en
  J_K_Flip_Flop j_k_ff_2 (
    .J(1'b1), .clk(j_k_ff_1_qn), .K(1'b1), .Q(BIT1), .Qn(j_k_ff_2_qn), .reset(out_2));  // open: preset, en
  J_K_Flip_Flop j_k_ff_3 (
    .J(1'b1), .clk(j_k_ff_2_qn), .K(1'b1), .Q(BIT2), .Qn(j_k_ff_3_qn), .reset(out_2));  // open: preset, en
  J_K_Flip_Flop j_k_ff_4 (.J(1'b1), .clk(j_k_ff_3_qn), .K(1'b1), .Q(BIT3), .reset(out_2));  // open: Qn, preset, en
endmodule

module Contador_9_0 (
  input  BIT3,
  input  BIT2,
  input  BIT1,
  input  BIT0,
  output A,
  output B,
  output C,
  output D,
  output E,
  output F,
  output G
);

  wire and_1_out, and_2_out, and_3_out, and_4_out, and_5_out, and_6_out, and_7_out, and_8_out, and_9_out,
       and_10_out, and_11_out, and_12_out, and_13_out, and_14_out, and_15_out, and_16_out, not_1_out,
       not_2_out, not_3_out, not_4_out, not_5_out, not_6_out, not_7_out, not_8_out, not_9_out, not_10_out,
       not_11_out, not_12_out, not_13_out, not_14_out, not_15_out, not_16_out, not_17_out, not_18_out,
       not_19_out, not_20_out, not_21_out, not_22_out, not_23_out;

  not not_1 (not_1_out, BIT3);
  and and_1 (and_1_out, not_1_out, not_2_out);
  not not_2 (not_2_out, BIT1);
  not not_3 (not_3_out, BIT3);
  and and_2 (and_2_out, not_3_out, BIT0);
  not not_4 (not_4_out, BIT3);
  and and_3 (and_3_out, not_4_out, not_5_out);
  not not_5 (not_5_out, BIT1);
  not not_6 (not_6_out, BIT2);
  and and_4 (and_4_out, not_6_out, BIT0);
  not not_7 (not_7_out, BIT3);
  and and_5 (and_5_out, not_7_out, not_8_out);
  not not_8 (not_8_out, BIT2);
  not not_9 (not_9_out, BIT3);
  and and_6 (and_6_out, not_9_out, not_10_out);
  not not_10 (not_10_out, BIT0);
  not not_11 (not_11_out, BIT2);
  and and_7 (and_7_out, not_11_out, BIT0);
  not not_12 (not_12_out, BIT2);
  and and_8 (and_8_out, not_12_out, not_13_out);
  not not_13 (not_13_out, BIT1);
  and and_9 (and_9_out, BIT1, not_14_out);
  not not_14 (not_14_out, BIT0);
  and and_10 (and_10_out, BIT2, BIT0);
  not not_15 (not_15_out, BIT2);
  or or_1 (E, not_15_out, not_16_out, not_17_out);
  not not_16 (not_16_out, BIT1);
  not not_17 (not_17_out, BIT0);
  not not_18 (not_18_out, BIT3);
  not not_19 (not_19_out, BIT2);
  and and_11 (and_11_out, not_18_out, not_19_out, not_20_out);
  not not_20 (not_20_out, BIT1);
  not not_21 (not_21_out, BIT2);
  and and_12 (and_12_out, not_21_out, BIT0);
  and and_13 (and_13_out, BIT2, not_22_out);
  not not_22 (not_22_out, BIT0);
  and and_14 (and_14_out, BIT2, BIT1);
  not not_23 (not_23_out, BIT2);
  and and_15 (and_15_out, not_23_out, BIT0);
  and and_16 (and_16_out, BIT1, BIT0);
  or or_2 (A, and_1_out, and_2_out, BIT2);
  or or_3 (B, and_3_out, and_4_out);
  or or_4 (C, and_5_out, and_6_out, and_7_out, BIT1);
  or or_5 (D, and_8_out, and_9_out, and_10_out);
  or or_6 (F, and_11_out, and_12_out, and_13_out, and_14_out);
  or or_7 (G, and_15_out, and_16_out);
endmodule
