// Logisim project Circuito.circ as structural Verilog: 1 circuit, main circuit main
module main (
);

  wire _1_out, _2_out, _3_out, _4_out, _5_out, A_out, and_1_out, and_2_out, and_3_out, and_4_out, and_5_out,
       and_6_out, and_7_out, and_8_out, and_9_out, and_10_out, and_11_out, and_12_out, and_13_out,
       and_14_out, and_15_out, and_16_out, and_17_out, and_18_out, and_19_out, and_20_out, and_21_out,
       and_22_out, BIT_0_out, BIT_1_out, BIT_2_out, BIT_3_out, L_out, or_1_out, or_2_out, or_3_out, or_4_out,
       or_5_out, or_6_out, or_7_out, u_out;

  Button _5 (.out(_5_out));
  Button u (.out(u_out));
  Button L (.out(L_out));
  Button _1 (.out(_1_out));
  Button A (.out(A_out));
  Button _3 (.out(_3_out));
  Button _2 (.out(_2_out));
  Button _4 (.out(_4_out));
  or BIT_0 (BIT_0_out, _4_out, A_out, _3_out);
  or BIT_1 (BIT_1_out, u_out, _2_out, _3_out);
  or BIT_2 (BIT_2_out, _1_out, A_out, _2_out, _3_out);
  buf BIT_3 (BIT_3_out, _5_out);  // OR_Gate
  and and_1 (and_1_out, ~BIT_2_out, BIT_3_out, ~_1_out);  // AND_Gate
  and and_2 (and_2_out, BIT_1_out, BIT_2_out);
  and and_3 (and_3_out, BIT_0_out, ~BIT_2_out);  // AND_Gate
  and and_4 (and_4_out, BIT_1_out, BIT_3_out);
  and and_5 (and_5_out, BIT_2_out, ~BIT_3_out);  // AND_Gate
  and and_6 (and_6_out, BIT_1_out, ~BIT_2_out);  // AND_Gate
  and and_7 (and_7_out, BIT_0_out, ~BIT_2_out);  // AND_Gate
  and and_8 (and_8_out, ~BIT_2_out, BIT_3_out);  // AND_Gate
  and and_9 (and_9_out, BIT_1_out, BIT_3_out);
  and and_10 (and_10_out, ~BIT_1_out, BIT_2_out, ~BIT_3_out);  // AND_Gate
  and and_11 (and_11_out, BIT_1_out, ~BIT_3_out);  // AND_Gate
  and and_12 (and_12_out, ~BIT_1_out, BIT_3_out);  // AND_Gate
  and and_13 (and_13_out, BIT_2_out, BIT_3_out);
  and and_14 (and_14_out, BIT_1_out, ~BIT_3_out);  // AND_Gate
  and and_15 (and_15_out, BIT_1_out, ~BIT_2_out);  // AND_Gate
  and and_16 (and_16_out, ~BIT_1_out, BIT_2_out, BIT_3_out);  // AND_Gate
  and and_17 (and_17_out, BIT_0_out, ~BIT_2_out);  // AND_Gate
  and and_18 (and_18_out, ~BIT_2_out, BIT_3_out);  // AND_Gate
  and and_19 (and_19_out, ~BIT_1_out, BIT_2_out, BIT_3_out);  // AND_Gate
  and and_20 (and_20_out, BIT_0_out, BIT_2_out);
  and and_21 (and_21_out, ~BIT_2_out, BIT_3_out);  // AND_Gate
  and and_22 (and_22_out, BIT_1_out, BIT_2_out);
  or or_1 (or_1_out, and_1_out, and_2_out);
  or or_2 (or_2_out, and_3_out, and_4_out, and_5_out);
  or or_3 (or_3_out, and_6_out, and_7_out, and_8_out, and_9_out, and_10_out);
  or or_4 (or_4_out, and_11_out, L_out, and_12_out, and_13_out);
  or or_5 (or_5_out, and_14_out, L_out, and_15_out, and_16_out);
  or or_6 (or_6_out, and_17_out, L_out, and_18_out, and_19_out);
  or or_7 (or_7_out, and_20_out, BIT_0_out, and_21_out, and_22_out);
  _7_Segment_Display u_7_segment_display_1 (
    .g(or_7_out), .f(or_6_out), .a(or_1_out), .b(or_2_out), .e(or_5_out), .d(or_4_out), .c(or_3_out));  // open: dp
endmodule
