// Logisim project Circuito 1.circ as structural Verilog: 2 circuits, main circuit main
module main (
);

  wire clock_1_out, j_k_ff_1_q, j_k_ff_1_qn, j_k_ff_2_q, j_k_ff_2_qn, j_k_ff_3_q, n7_seg_1_a, n7_seg_1_b,
       n7_seg_1_c, n7_seg_1_d, n7_seg_1_e, n7_seg_1_f, n7_seg_1_g;

  Clock clock_1 (.out(clock_1_out));
  J_K_Flip_Flop j_k_ff_1 (
    .J(j_k_ff_2_q), .clk(clock_1_out), .K(j_k_ff_2_q), .Q(j_k_ff_1_q), .Qn(j_k_ff_1_qn));  // open: preset, en, reset
  J_K_Flip_Flop j_k_ff_2 (
    .J(j_k_ff_2_qn), .clk(clock_1_out), .K(j_k_ff_2_q), .Q(j_k_ff_2_q), .Qn(j_k_ff_2_qn));  // open: preset, en, reset
  J_K_Flip_Flop j_k_ff_3 (
    .J(j_k_ff_1_q), .clk(clock_1_out), .K(j_k_ff_1_qn), .Q(j_k_ff_3_q));  // open: Qn, preset, en, reset
  _7_seg u_7_seg_1 (
    .A1(1'b0), .A2(j_k_ff_1_q), .A3(j_k_ff_2_q), .A4(j_k_ff_3_q), .a(n7_seg_1_a), .b(n7_seg_1_b),
    .c(n7_seg_1_c), .d(n7_seg_1_d), .e(n7_seg_1_e), .f(n7_seg_1_f), .g(n7_seg_1_g));
  _7_Segment_Display u_7_segment_display_1 (
    .g(n7_seg_1_a), .f(n7_seg_1_b), .a(n7_seg_1_c), .b(n7_seg_1_d), .e(n7_seg_1_g), .d(n7_seg_1_f),
    .c(n7_seg_1_e));  // open: dp
endmodule

module _7_seg (
  input  A1,
  input  A2,
  input  A3,
  input  A4,
  output a,
  output b,
  output c,
  output d,
  output e,
  output f,
  output g
);

  wire and_1_out, and_2_out, and_3_out, and_4_out, and_5_out, and_6_out, and_7_out, and_8_out, and_9_out,
       and_10_out, and_11_out, and_12_out, and_13_out, and_14_out, and_15_out, and_16_out, and_17_out,
       and_18_out, and_19_out, and_20_out, and_21_out, and_22_out, and_23_out, and_24_out, and_25_out,
       and_26_out, not_1_out, not_2_out, not_3_out, not_4_out, not_5_out, not_6_out, not_7_out, not_8_out,
       not_9_out, not_10_out, not_11_out, not_12_out, not_13_out, not_14_out, not_15_out, not_16_out,
       not_17_out, not_18_out, not_19_out, not_20_out, not_21_out, not_22_out, not_23_out, not_24_out,
       not_25_out, not_26_out, not_27_out, not_28_out, not_29_out, not_30_out, not_31_out, not_32_out,
       not_33_out, not_34_out, not_35_out, not_36_out, not_37_out, not_38_out, not_39_out, not_40_out,
       not_41_out, not_42_out, not_43_out, not_44_out, not_45_out, not_46_out, not_47_out, not_48_out,
       not_49_out, not_50_out, not_51_out, not_52_out;

  not not_1 (not_1_out, A1);
  not not_2 (not_2_out, A2);
  and and_1 (and_1_out, not_1_out, not_2_out, not_3_out);
  not not_3 (not_3_out, A4);
  not not_4 (not_4_out, A1);
  and and_2 (and_2_out, not_4_out, A3);
  not not_5 (not_5_out, A1);
  and and_3 (and_3_out, not_5_out, A2, A4);
  not not_6 (not_6_out, A2);
  and and_4 (and_4_out, A1, not_6_out, not_7_out);
  not not_7 (not_7_out, A3);
  not not_8 (not_8_out, A1);
  and and_5 (and_5_out, not_8_out, not_9_out);
  not not_9 (not_9_out, A2);
  not not_10 (not_10_out, A1);
  and and_6 (and_6_out, not_10_out, not_11_out, not_12_out);
  not not_11 (not_11_out, A3);
  not not_12 (not_12_out, A4);
  not not_13 (not_13_out, A2);
  and and_7 (and_7_out, not_13_out, not_14_out);
  not not_14 (not_14_out, A3);
  not not_15 (not_15_out, A1);
  and and_8 (and_8_out, not_15_out, A3, A4);
  not not_16 (not_16_out, A2);
  and and_9 (and_9_out, not_16_out, not_17_out);
  not not_17 (not_17_out, A3);
  not not_18 (not_18_out, A1);
  and and_10 (and_10_out, not_18_out, A4);
  not not_19 (not_19_out, A1);
  and and_11 (and_11_out, not_19_out, A2);
  not not_20 (not_20_out, A1);
  not not_21 (not_21_out, A2);
  not not_22 (not_22_out, A4);
  not not_23 (not_23_out, A1);
  not not_24 (not_24_out, A2);
  not not_25 (not_25_out, A1);
  not not_26 (not_26_out, A4);
  not not_27 (not_27_out, A1);
  not not_28 (not_28_out, A3);
  not not_29 (not_29_out, A2);
  not not_30 (not_30_out, A3);
  not not_31 (not_31_out, A2);
  not not_32 (not_32_out, A3);
  and and_12 (and_12_out, not_31_out, not_32_out, not_33_out);
  not not_33 (not_33_out, A4);
  not not_34 (not_34_out, A1);
  and and_13 (and_13_out, not_34_out, A3, not_35_out);
  not not_35 (not_35_out, A4);
  not not_36 (not_36_out, A1);
  and and_14 (and_14_out, not_36_out, not_37_out, not_38_out);
  not not_37 (not_37_out, A3);
  not not_38 (not_38_out, A4);
  not not_39 (not_39_out, A1);
  and and_15 (and_15_out, not_39_out, A2, not_40_out);
  not not_40 (not_40_out, A3);
  not not_41 (not_41_out, A1);
  and and_16 (and_16_out, not_41_out, A2, not_42_out);
  not not_42 (not_42_out, A4);
  and and_17 (and_17_out, A1, not_43_out, not_44_out);
  not not_43 (not_43_out, A2);
  not not_44 (not_44_out, A3);
  not not_45 (not_45_out, A1);
  and and_18 (and_18_out, not_45_out, not_46_out, A3);
  not not_46 (not_46_out, A2);
  not not_47 (not_47_out, A1);
  and and_19 (and_19_out, not_47_out, A2, not_48_out);
  not not_48 (not_48_out, A3);
  not not_49 (not_49_out, A1);
  and and_20 (and_20_out, not_49_out, A2, not_50_out);
  not not_50 (not_50_out, A4);
  and and_21 (and_21_out, A1, not_51_out, not_52_out);
  not not_51 (not_51_out, A2);
  not not_52 (not_52_out, A3);
  or or_1 (a, and_1_out, and_2_out, and_3_out, and_4_out);
  or or_2 (b, and_5_out, and_6_out, and_7_out, and_8_out);
  or or_3 (c, and_9_out, and_10_out, and_11_out);
  and and_22 (and_22_out, not_20_out, not_21_out, not_22_out);
  and and_23 (and_23_out, not_23_out, not_24_out, A3);
  and and_24 (and_24_out, not_25_out, A3, not_26_out);
  and and_25 (and_25_out, not_27_out, A2, not_28_out, A4);
  and and_26 (and_26_out, A1, not_29_out, not_30_out);
  or or_4 (e, and_12_out, and_13_out);
  or or_5 (f, and_14_out, and_15_out, and_16_out, and_17_out);
  or or_6 (g, and_18_out, and_19_out, and_20_out, and_21_out);
  or or_7 (d, and_22_out, and_23_out, and_24_out, and_25_out, and_26_out);
endmodule
