// Logisim project Circuito COD-DECOD.circ as structural Verilog: 1 circuit, main circuit main
module main (
  input  _9,
  input  _8,
  input  _7,
  input  _6,
  input  _5,
  input  _4,
  input  _3,
  input  _2,
  input  _1,
  input  _0,
  input  A,
  input  B,
  input  C,
  input  D,
  output out_15,
  output out_16,
  output out_17,
  output out_18,
  output out_19,
  output out_20,
  output out_21,
  output out_22,
  output out_23,
  output out_24,
  output out_25
);

  wire and_1_out, and_2_out, and_3_out, and_4_out, and_5_out, and_6_out, and_7_out, and_8_out, and_9_out,
       and_10_out, and_11_out, and_12_out, and_13_out, and_14_out, and_15_out, and_16_out, and_17_out;

  and and_1 (and_1_out, B, D);
  and and_2 (and_2_out, ~B, ~D);  // AND_Gate
  and and_3 (and_3_out, ~C, ~D);  // AND_Gate
  and and_4 (and_4_out, C, D);
  and and_5 (and_5_out, C, D);
  and and_6 (and_6_out, ~B, ~D);  // AND_Gate
  and and_7 (and_7_out, C, ~D);  // AND_Gate
  and and_8 (and_8_out, ~A, ~B, C);  // AND_Gate
  and and_9 (and_9_out, ~A, B, ~C, D);  // AND_Gate
  and and_10 (and_10_out, ~B, D);  // AND_Gate
  and and_11 (and_11_out, C, ~D);  // AND_Gate
  and and_12 (and_12_out, ~C, ~D);  // AND_Gate
  and and_13 (and_13_out, ~A, B, ~C);  // AND_Gate
  and and_14 (and_14_out, ~A, B, ~D);  // AND_Gate
  and and_15 (and_15_out, C, ~D);  // AND_Gate
  and and_16 (and_16_out, ~A, ~B, C);  // AND_Gate
  buf and_17 (and_17_out, ~C);  // AND_Gate AND_Gate
  or or_1 (out_15, _9, _8);
  or or_2 (out_16, _7, _6, _5, _4);
  or or_3 (out_17, _7, _6, _3, _2);
  or or_4 (out_18, _9, _7, _5, _3, _1);
  or or_5 (out_19, C, A, and_1_out, and_2_out);
  or or_6 (out_20, ~B, and_3_out, and_4_out);  // OR_Gate
  or or_7 (out_21, ~C, B, and_5_out);  // OR_Gate
  or or_8 (out_22, A, and_6_out, and_7_out, and_8_out, and_9_out);
  or or_9 (out_23, and_10_out, and_11_out);
  or or_10 (out_24, A, and_12_out, and_13_out, and_14_out);
  or or_11 (out_25, A, and_15_out, and_16_out, and_17_out);
  _7_Segment_Display u_7_segment_display_1 (
    .g(out_23), .f(out_24), .a(out_19), .b(out_20), .e(out_25), .d(out_22), .c(out_21));  // open: dp

  // Notes on the sheet:
  //   CODIFICADOR DECIMAL BINÁRIO
  //   CODIFICADOR BINÁRIO - 7 SEGUIMENTOS
endmodule
