// Logisim project Circuito Memória RAM.circ as structural Verilog: 1 circuit, main circuit main
module main (
  input  [7:0] Input
);

  wire Clear_RAM_out, Clock_IN_out, Clock_INPUT_out, Clock_Marcador_out, Clock_RAM_out, Clock_Saida_out,
       Leitura_RAM_out;
  wire [7:0] IN_q, ram_1_data, register_1_q;

  Clock Clock_Marcador (.out(Clock_Marcador_out));
  Clock Clock_RAM (.out(Clock_RAM_out));
  Clock Leitura_RAM (.out(Leitura_RAM_out));
  Clock Clear_RAM (.out(Clear_RAM_out));
  Clock Clock_INPUT (.out(Clock_INPUT_out));
  Clock Clock_IN (.out(Clock_IN_out));
  Clock Clock_Saida (.out(Clock_Saida_out));
  Register register_1 (.D(ram_1_data), .Q(register_1_q), .clk(Clock_Marcador_out));  // open: en, clr
  RAM ram_1 (
    .addr(register_1_q), .data(ram_1_data), .clk(Clock_RAM_out), .ld(Leitura_RAM_out), .clr(Clear_RAM_out));  // open: sel
  Register IN (.D(Input), .Q(IN_q), .clk(Clock_INPUT_out));  // open: en, clr
  assign ram_1_data = Clock_IN_out ? IN_q : 8'bz;  // Controlled_Buffer controlled_buffer_1
  Register Output (.D(ram_1_data), .clk(Clock_Saida_out));  // open: en, Q, clr

  // Notes on the sheet:
  //   MARCADOR
  //   ENTRADA
  //   RAM
  //   SAÍDA
endmodule
