// Logisim project Circuito Somador.circ as structural Verilog: 1 circuit, main circuit main
module main (
  input  A,
  input  B,
  input  ENTRADA,
  input  A_2,
  input  B_2,
  input  A_3,
  input  B_3,
  input  A_4,
  input  B_4,
  output SOMA,
  output SOMA_2,
  output SOMA_3,
  output SOMA_4,
  output SAIDA
);

  wire and_1_out, and_2_out, and_3_out, and_4_out, and_5_out, and_6_out, and_7_out, and_8_out, xor_1_out,
       xor_2_out, xor_3_out, xor_4_out, xor_9_out, xor_10_out, xor_11_out;

  xor xor_1 (xor_1_out, A, B);
  and and_1 (and_1_out, A, B);
  xor xor_2 (xor_2_out, A_2, B_2);
  and and_2 (and_2_out, A_2, B_2);
  xor xor_3 (xor_3_out, A_3, B_3);
  and and_3 (and_3_out, A_3, B_3);
  xor xor_4 (xor_4_out, A_4, B_4);
  and and_4 (and_4_out, A_4, B_4);
  xor xor_5 (SOMA, xor_1_out, ENTRADA);
  and and_5 (and_5_out, xor_1_out, ENTRADA);
  xor xor_6 (SOMA_2, xor_2_out, xor_9_out);
  and and_6 (and_6_out, xor_2_out, xor_9_out);
  xor xor_7 (SOMA_3, xor_3_out, xor_10_out);
  and and_7 (and_7_out, xor_3_out, xor_10_out);
  xor xor_8 (SOMA_4, xor_4_out, xor_11_out);
  and and_8 (and_8_out, xor_4_out, xor_11_out);
  xor xor_9 (xor_9_out, and_1_out, and_5_out);
  xor xor_10 (xor_10_out, and_2_out, and_6_out);
  xor xor_11 (xor_11_out, and_3_out, and_7_out);
  xor xor_12 (SAIDA, and_4_out, and_8_out);
endmodule
